# Fritzing sketch minitron (saved by Fritzing 0.9.3b)
breadboards: 1

parts:
  Part1 = Adafruit CharliePlex Driver IS31FL3731 [part_number="Adafruit #2946"]
  Part2 = Arduino Uno (Rev3)
  S1 = Pushbutton [package="[THT]"]
  R1 = Resistor [tolerance=±5% resistance=220 package=THT]

nets:
  GND: Part1.GND, Part2.GND, Part2.D6_PWM, S1.Pin_1, S1.Pin_2, S1.Pin_3, S1.Pin_4, R1.Pin_1
  N1: Part1.SCL, Part2.A5/SCL
  N2: Part1.SDA, Part2.A4/SDA
  VCC: Part1.VCC, Part2.5V, R1.Pin_0

custom parts:
  Adafruit CharliePlex Driver IS31FL3731: The IS31FL3731 will let you get back to that classic LED matrix look, with a nice upgrade! This I2C LED driver chip has the ability to PWM each individual LED in a 16x9 grid so you can have beautiful LED lighting effects, without a lot of pin twiddling. Simply tell the chip which LED on the grid you want lit, and what brightness and it's all taken care of for you. The IS31FL3731 is a nice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
